# Fritzing sketch LabDCMotorH-BridgeSwitch (saved by Fritzing 0.9.0b)
breadboards: 1

parts:
  Arduino = Arduino Uno (Rev3)
  S1 = Toggle Switch [package=THT]
  R1 = Resistor [tolerance=±5% resistance=10k package=THT]

nets:
  N1: Arduino.D2, S1.L2, R1.Pin_1
  N2: Arduino.5V, S1.COM
  GND: Arduino.GND, R1.Pin_0
