# Fritzing sketch LabHighCurrentLoad (saved by Fritzing 0.9.0b)
breadboards: 1

parts:
  Power_plug1 = Power plug
  IC2 = Voltage Regulator [package=78xxl]

nets:
  GND: Power_plug1.GND, IC2.GND
  N1: Power_plug1.VCC, IC2.IN
