# Fritzing sketch LabHighCurrentLoadLightBulb (saved by Fritzing 0.9.0b)
breadboards: 1

parts:
  Power_Plug = Power plug
  Voltage_Regulator = Voltage Regulator [package=78xxl]
  DC_Motor = DC Motor
  TIP_120_Transistor = npn-Powertransistor [package="TO220 [THT]"]
  Resistor = Resistor [tolerance=±5% resistance=1k package=THT]
  S1 = Pushbutton [package="[THT]"]

nets:
  GND: Power_Plug.GND, Voltage_Regulator.GND, TIP_120_Transistor.emitter
  N1: Power_Plug.VCC, Voltage_Regulator.IN, DC_Motor.pin_2
  N2: Voltage_Regulator.OUT, Resistor.Pin_1, S1.Pin_1, S1.Pin_2
  N3: DC_Motor.pin_1, TIP_120_Transistor.collector
  N4: TIP_120_Transistor.base, Resistor.Pin_0
  N5: S1.Pin_3, S1.Pin_4
