# Fritzing sketch LabHighCurrentLoadPotentiometer (saved by Fritzing 0.9.0b)
breadboards: 1

parts:
  Power_Plug = Power plug
  Voltage_Regulator = Voltage Regulator [package=78xxl]
  DC_Motor = DC Motor
  TIP_120_Transistor = npn-Powertransistor [package="TO220 [THT]"]
  Resistor = Resistor [tolerance=±5% resistance=1k package=THT]
  Diode = Rectifier Diode [part_number=1N4001 package="Melf DO-213 AB [SMD]"]
  Potentiometer = POT [package=alps_pot]

nets:
  GND: Power_Plug.GND, Voltage_Regulator.GND, TIP_120_Transistor.emitter, Diode.anode, Potentiometer.A
  N1: Power_Plug.VCC, Voltage_Regulator.IN, DC_Motor.pin_2
  N2: Voltage_Regulator.OUT, Potentiometer.E
  N3: DC_Motor.pin_1, TIP_120_Transistor.collector, Diode.cathode
  N4: TIP_120_Transistor.base, Resistor.Pin_0
  N5: Resistor.Pin_1, Potentiometer.S
