# Fritzing sketch LabHighCurrentArduinoMotor (saved by Fritzing 0.9.0b)
breadboards: 1

parts:
  Arduino1 = Arduino Uno (Rev3)
  Potentiometer = POT [package=alps_pot]
  TIP_120_Transistor1 = npn-Powertransistor [package="TO220 [THT]"]
  Motor = DC Motor
  Power_Plug = Power plug
  Diode = Rectifier Diode [part_number=1N4001 package="Melf DO-213 AB [SMD]"]

nets:
  N1: Arduino1.A0, Potentiometer.S
  N2: Arduino1.D8, TIP_120_Transistor1.base
  N3: Arduino1.5V, Potentiometer.E
  GND: Arduino1.GND, Potentiometer.A, TIP_120_Transistor1.emitter, Power_Plug.GND, Diode.anode
  N4: TIP_120_Transistor1.collector, Motor.pin_2, Diode.cathode
  N5: Motor.pin_1, Power_Plug.VCC
