# Fritzing sketch LabHighCurrentArduinoTransistor (saved by Fritzing 0.9.0b)
breadboards: 1

parts:
  Arduino1 = Arduino Uno (Rev3)
  Potentiometer = POT [package=alps_pot]
  TIP_120_Transistor1 = npn-Powertransistor [package="TO220 [THT]"]

nets:
  N1: Arduino1.A0, Potentiometer.S
  N2: Arduino1.D8, TIP_120_Transistor1.base
  N3: Arduino1.5V, Potentiometer.E
  GND: Arduino1.GND, Potentiometer.A, TIP_120_Transistor1.emitter
