# Fritzing sketch LabStepperMotorH-BridgeStepper (saved by Fritzing 0.9.0b)
breadboards: 1

parts:
  Arduino = Arduino Uno (Rev3)
  L293_H-Bridge = H-Bridge [package=THT]
  Power_Plug = Power plug

nets:
  N1: Arduino.D3_PWM, L293_H-Bridge.2A
  N2: Arduino.5V, L293_H-Bridge.1_2EN, L293_H-Bridge.3_4EN, L293_H-Bridge.VCC1
  GND: Arduino.GND, L293_H-Bridge.GND1, L293_H-Bridge.GND2, L293_H-Bridge.GND3, L293_H-Bridge.GND4, Power_Plug.GND
  N3: L293_H-Bridge.VCC2, Power_Plug.VCC
