# Fritzing sketch LabStepperMotorH-BridgeStepperWiring (saved by Fritzing 0.9.0b)
breadboards: 1

parts:
  Arduino = Arduino Uno (Rev3)
  L293_H-Bridge = H-Bridge [package=THT]
  Power_Plug = Power plug
  M1 = Stepper Motor - Unipolar

nets:
  N1: Arduino.5V, L293_H-Bridge.1_2EN, L293_H-Bridge.3_4EN, L293_H-Bridge.VCC1
  GND: Arduino.GND, L293_H-Bridge.GND1, L293_H-Bridge.GND2, L293_H-Bridge.GND3, L293_H-Bridge.GND4, Power_Plug.GND
  N2: L293_H-Bridge.1Y, M1.B
  N3: L293_H-Bridge.2Y, M1.COMMON_1
  N4: L293_H-Bridge.VCC2, Power_Plug.VCC
  N5: L293_H-Bridge.3Y, M1.C
  N6: L293_H-Bridge.4Y, M1.COMMON_2
