# Fritzing sketch LabStepperMotorH-BridgeStepperWiringToArduino (saved by Fritzing 0.9.0b)
breadboards: 1

parts:
  Arduino = Arduino Uno (Rev3)
  L293_H-Bridge = H-Bridge [package=THT]
  Power_Plug = Power plug
  M1 = Stepper Motor - Unipolar

nets:
  N1: Arduino.D8, L293_H-Bridge.1A
  N2: Arduino.D9_PWM, L293_H-Bridge.2A
  N3: Arduino.D10_PWM/SS, L293_H-Bridge.3A
  N4: Arduino.D11_PWM/MOSI, L293_H-Bridge.4A
  N5: Arduino.5V, L293_H-Bridge.1_2EN, L293_H-Bridge.3_4EN, L293_H-Bridge.VCC1
  GND: Arduino.GND, L293_H-Bridge.GND1, L293_H-Bridge.GND2, L293_H-Bridge.GND3, L293_H-Bridge.GND4, Power_Plug.GND
  N6: L293_H-Bridge.1Y, M1.B
  N7: L293_H-Bridge.2Y, M1.COMMON_1
  N8: L293_H-Bridge.VCC2, Power_Plug.VCC
  N9: L293_H-Bridge.3Y, M1.C
  N10: L293_H-Bridge.4Y, M1.COMMON_2
